// Logisim project HomeSecuritySystem.circ as structural Verilog: 1 circuit, main circuit main
module main (
);

  wire A, ALA, ALARM2, and_2_out, BR, Check, clock_1_out, clock_2_out, clock_3_out, CP, d_ff_1_q, d_ff_2_q,
       ICP, K, L, LR, not_1_out, not_2_out, not_3_out, or_1_out, pass, xnor_1_out, xnor_2_out, xnor_3_out,
       xnor_4_out;
  wire [1:0] j_k_ff_1_q;

  LED led_1 (.in(L));
  LED led_2 (.in(L));
  LED led_3 (.in(BR));
  LED led_4 (.in(BR));
  LED led_5 (.in(ALARM2));
  LED led_6 (.in(ALA));
  LED led_7 (.in(CP));
  LED led_8 (.in(L));
  LED led_9 (.in(L));
  Button button_1 (.out(Check));
  LED led_10 (.in(K));
  LED led_11 (.in(K));
  LED led_12 (.in(LR));
  LED led_13 (.in(LR));
  LED led_14 (.in(1'b1));
  LED led_15 (.in(1'b1));
  LED led_16 (.in(1'b1));
  LED led_17 (.in(1'b1));
  LED led_18 (.in(1'b1));
  LED led_19 (.in(1'b1));
  not not_1 (not_1_out, pass);
  Clock clock_1 (.out(clock_1_out));
  not not_2 (not_2_out, clock_1_out);
  and and_1 (A, Check, not_1_out);
  and and_2 (and_2_out, Check, pass);
  J_K_Flip_Flop j_k_ff_1 (.J(A), .clk(not_2_out), .K(A), .Q(j_k_ff_1_q[0]), .reset(CP));  // open: Qn, preset, en
  not not_3 (not_3_out, j_k_ff_1_q[0]);
  Clock clock_2 (.out(clock_2_out));
  Clock clock_3 (.out(clock_3_out));
  J_K_Flip_Flop j_k_ff_2 (.J(A), .clk(not_3_out), .K(A), .Q(j_k_ff_1_q[1]), .reset(CP));  // open: Qn, preset, en
  xnor xnor_1 (xnor_1_out, 1'b1, 1'b1);
  xnor xnor_2 (xnor_2_out, 1'b1, 1'b1);
  xnor xnor_3 (xnor_3_out, 1'b0, 1'b1);
  xnor xnor_4 (xnor_4_out, 1'b0, 1'b0);
  D_Flip_Flop d_ff_1 (.clk(clock_2_out), .D(A), .Q(d_ff_1_q));  // open: Qn, preset, en, reset
  D_Flip_Flop d_ff_2 (.clk(clock_3_out), .D(and_2_out), .Q(d_ff_2_q));  // open: Qn, preset, en, reset
  Hex_Digit_Display hex_digit_display_1 (.value({2'b00, j_k_ff_1_q}));  // open: dp
  and and_3 (pass, xnor_1_out, xnor_2_out, xnor_3_out, xnor_4_out);
  D_Flip_Flop d_ff_3 (.clk(d_ff_1_q), .D(A), .Q(ICP), .reset(and_2_out));  // open: Qn, preset, en
  D_Flip_Flop d_ff_4 (.clk(d_ff_2_q), .D(and_2_out), .Q(CP), .reset(A));  // open: Qn, preset, en
  and and_4 (ALA, j_k_ff_1_q[0], j_k_ff_1_q[1]);
  // Probe on pass
  or or_1 (or_1_out, 1'b0, 1'b1, 1'b0, 1'b0);
  and and_5 (BR, 1'b0, CP);
  and and_6 (L, 1'b0, CP);
  and and_7 (K, 1'b0, CP);
  and and_8 (LR, 1'b1, CP);
  and and_9 (ALARM2, or_1_out, ICP);

  // Notes on the sheet:
  //   BED_ROOM
  //   LOUNGE
  //   ENTERANCE
  //   unlocked
  //   DIGITAL HOME SECURITY SYSTEM
  //   ENTERED PASSWORD
  //   LIVING_ROOM
  //   KITCHEN
  //   FAN
  //   COUNTER ALARM
  //   AC
  //   BULB
  //   ALARM MOTION DETECTION 
  //   CORRECT PASSWORT
  //   COUNTER
  //   SAVED PASSWORD
  //   CORRECT-INCORRECT PASSWORD LOGIC
  //   MSB
  //   MOVEMENT DETECTION WITH INCORRECT PASSWORD
  //   MOVEMENT DETECTION WITH CORRECT PASSWORD
endmodule
